# Fritzing sketch Midterm-2-Fritzing (saved by Fritzing 0.9.9b)
breadboards: 1

parts:
  Argon1 = Particle Argon
  OLED_I2C1 = OLED 128x64 I2C Monochrome Display
  SENS1 = SoilWatch 10
  M1 = BMP280
  Relay1 = Relay - 6 pins [package="DIP (Dual Inline) [THT]"]
  M2 = DC Motor
  Q1 = PNP-Transistor [package="TO92 [THT]"]
  R1 = Resistor [tolerance=±5% resistance=220 package="0402 [SMD]"]
  R2 = Resistor [tolerance=±5% resistance=220 package="2010 [SMD]"]
  Part1 = MQ-131 breakout
  Grove1 = Grove Dust Sensor

nets:
  VCC: Argon1.3.3V, OLED_I2C1.VDD, SENS1.VCC, M1.VIN, Relay1.VCC, Part1.AO, Grove1.VCC
  GND: Argon1.GND, OLED_I2C1.GND, SENS1.GND, M1.GND, Relay1.GND, M2.pin_2, Q1.B, R2.Pin_0, Part1.DO, Grove1.GND
  N1: Argon1.A1, SENS1.OUT
  N2: Argon1.A2, Grove1.SIG
  N3: Argon1.A3, Part1.GND
  N4: Argon1.SCK, OLED_I2C1.SCK, M1.SCL
  N5: Argon1.MI, Q1.C, R2.Pin_1
  N6: Argon1.SDA, OLED_I2C1.SDA, M1.SDA
  N7: Relay1.IN, Q1.E, R1.Pin_0
  N8: Relay1.COM, M2.pin_1
  N9: Relay1.ON, R1.Pin_1

custom parts:
  Particle Argon: The Argon is a powerful Wi-Fi enabled development board that can act as either a standalone Wi-Fi endpoint or Wi-Fi enabled gateway for Particle Mesh networks. It is based on the Nordic nRF52840 and has built-in battery charging circuitry so it’s easy to connect a Li-Po and deploy your local network in minutes. The Argon is great for connecting existing projects to the Particle Device Cloud or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
  SoilWatch 10: SoilWatch 10 - Capacitive soil moisture sensor
  BMP280: Temperature Humidity Barometric presure Sensor, I2C
  Relay - 6 pins: A DIP stand-in part for whatever IC you want. With 6 pins on a 900mil dual inline package (DIP) footprint.
  MQ-131 breakout: SKU: 101282
  Grove Dust Sensor: PPD42 Grove Dust Sensor
